# Fritzing sketch project (saved by Fritzing 0.9.0b)
breadboards: 1

parts:
  Raspberry_Pi1 = Raspberry Pi 2
  R1 = Resistor [tolerance=±5% resistance=68 package=THT]
  LED1 = smd LED [color="Blue (430nm)" package="0805 [SMD]"]
  LED2 = smd LED [color="Green (555nm)" package="0805 [SMD]"]
  R2 = Resistor [tolerance=±5% resistance=4.6 package=THT]

nets:
  N1: Raspberry_Pi1.GND, LED1.cathode, LED2.anode
  N2: Raspberry_Pi1.GPIO24, R2.Pin_1
  N3: Raspberry_Pi1.GPIO23, R1.Pin_1
  N4: R1.Pin_0, LED2.cathode
  N5: LED1.anode, R2.Pin_0
